// Logisim project stage3.circ.circ as structural Verilog: 3 circuits, main circuit main
module main (
);

  wire button_2_out, button_3_out, clock_1_out, stage2_1_a1, stage2_1_a2, t_ff_1_q;
  wire [3:0] stage2_1_out_4, stage3_1_out_6;

  Button button_1 ();  // open: out
  Clock clock_1 (.out(clock_1_out));
  Button button_2 (.out(button_2_out));
  T_Flip_Flop t_ff_1 (.T(button_2_out), .clk(button_2_out), .Q(t_ff_1_q));  // open: Qn, reset, preset
  Button button_3 (.out(button_3_out));
  stage2 stage2_1 (
    .Reset(button_3_out), .Connection(t_ff_1_q), .Clock(clock_1_out), .out_4(stage2_1_out_4),
    .A1(stage2_1_a1), .A2(stage2_1_a2));
  stage3 stage3_1 (
    .Clock(clock_1_out), .Connection(t_ff_1_q), .Reset(button_3_out), .A1(stage2_1_a1), .A2(stage2_1_a2),
    .out_6(stage3_1_out_6));
  LED led_1 ();  // open: in
  Hex_Digit_Display hex_digit_display_1 ();  // open: value, dp
  Hex_Digit_Display hex_digit_display_2 ();  // open: value, dp
  Hex_Digit_Display hex_digit_display_3 (.value(stage3_1_out_6));  // open: dp
  Hex_Digit_Display hex_digit_display_4 (.value(stage2_1_out_4));  // open: dp
  Hex_Digit_Display hex_digit_display_5 ();  // open: value, dp
  Hex_Digit_Display hex_digit_display_6 ();  // open: value, dp
  Hex_Digit_Display hex_digit_display_7 ();  // open: value, dp
  Hex_Digit_Display hex_digit_display_8 ();  // open: value, dp

  // Notes on the sheet:
  //   Split
  //   Start/Stop
  //   Stopwatch Interface
  //   Reset
  //   Clock started
  //   Elapsed Time
  //   .
  //   .
  //   Split Time
  //   .
  //   .
endmodule

module stage2 (
  input  Reset,
  input  Connection,
  input  Clock,
  output [3:0] out_4,
  output A1,
  output A2
);

  wire and_1_out, and_2_out, and_3_out, and_4_out, and_5_out, j_k_ff_1_q, j_k_ff_3_q, or_1_out;

  J_K_Flip_Flop j_k_ff_1 (
    .J(Connection), .K(Connection), .clk(Clock), .Q(j_k_ff_1_q), .reset(or_1_out));  // open: Qn, preset
  and and_1 (and_1_out, Clock, Connection);
  and and_2 (and_2_out, Connection, j_k_ff_1_q);
  J_K_Flip_Flop j_k_ff_2 (.J(and_2_out), .K(and_2_out), .clk(Clock), .Q(A1), .reset(or_1_out));  // open: Qn, preset
  D_Flip_Flop d_ff_1 (.D(j_k_ff_1_q), .clk(and_1_out), .Q(out_4[0]));  // open: Qn, preset, reset
  and and_3 (and_3_out, and_2_out, A1);
  D_Flip_Flop d_ff_2 (.D(A1), .clk(and_1_out), .Q(out_4[1]));  // open: Qn, preset, reset
  J_K_Flip_Flop j_k_ff_3 (
    .J(and_3_out), .K(and_3_out), .clk(Clock), .Q(j_k_ff_3_q), .reset(or_1_out));  // open: Qn, preset
  and and_4 (and_4_out, and_3_out, j_k_ff_3_q);
  D_Flip_Flop d_ff_3 (.D(j_k_ff_3_q), .clk(and_1_out), .Q(out_4[2]));  // open: Qn, preset, reset
  J_K_Flip_Flop j_k_ff_4 (.J(and_4_out), .K(and_4_out), .clk(Clock), .Q(A2), .reset(or_1_out));  // open: Qn, preset
  D_Flip_Flop d_ff_4 (.D(A2), .clk(and_1_out), .Q(out_4[3]));  // open: Qn, preset, reset
  and and_5 (and_5_out, A1, A2);
  or or_1 (or_1_out, and_5_out, Reset);
endmodule

module stage3 (
  input  Clock,
  input  Connection,
  input  Reset,
  input  A1,
  input  A2,
  output [3:0] out_6
);

  wire and_1_out, and_2_out, and_3_out, and_4_out, j_k_ff_1_q, j_k_ff_2_q, j_k_ff_3_q, or_1_out;

  and and_1 (and_1_out, Clock, Connection);
  and and_2 (and_2_out, A1, A2);
  J_K_Flip_Flop j_k_ff_1 (
    .J(and_2_out), .K(and_2_out), .clk(and_2_out), .Q(j_k_ff_1_q), .reset(or_1_out));  // open: Qn, preset
  D_Flip_Flop d_ff_1 (.D(j_k_ff_1_q), .clk(and_1_out), .Q(out_6[0]), .reset(Reset));  // open: Qn, preset
  J_K_Flip_Flop j_k_ff_2 (
    .J(j_k_ff_1_q), .K(j_k_ff_1_q), .clk(and_2_out), .Q(j_k_ff_2_q), .reset(or_1_out));  // open: Qn, preset
  and and_3 (and_3_out, j_k_ff_2_q, j_k_ff_1_q);
  D_Flip_Flop d_ff_2 (.D(j_k_ff_2_q), .clk(and_1_out), .Q(out_6[1]), .reset(Reset));  // open: Qn, preset
  J_K_Flip_Flop j_k_ff_3 (
    .J(and_3_out), .K(and_3_out), .clk(and_2_out), .Q(j_k_ff_3_q), .reset(or_1_out));  // open: Qn, preset
  and and_4 (and_4_out, j_k_ff_3_q, j_k_ff_2_q);
  or or_1 (or_1_out, and_4_out, Reset);
  D_Flip_Flop d_ff_3 (.D(j_k_ff_3_q), .clk(and_1_out), .Q(out_6[2]), .reset(Reset));  // open: Qn, preset

  assign out_6[3] = 1'b0;
endmodule
