// Logisim project stage4.circ.circ as structural Verilog: 4 circuits, main circuit main
module main (
);

  wire button_2_out, button_3_out, clock_1_out, stage2_1_a1, stage2_1_a2, stage3_1_b1, stage3_1_b2,
       stage3_1_b3, stage4_1_c1, stage4_1_c2, stage4_1_reset, t_ff_1_q;
  wire [3:0] stage2_1_out_4, stage3_1_out_7, stage4_1_out_7, stage4_2_out_7;

  Button button_1 ();  // open: out
  Clock clock_1 (.out(clock_1_out));
  Button button_2 (.out(button_2_out));
  T_Flip_Flop t_ff_1 (.T(button_2_out), .clk(button_2_out), .Q(t_ff_1_q));  // open: Qn, reset, preset
  Button button_3 (.out(button_3_out));
  stage2 stage2_1 (
    .Reset(button_3_out), .Connection(t_ff_1_q), .Clock(clock_1_out), .out_4(stage2_1_out_4),
    .A1(stage2_1_a1), .A2(stage2_1_a2));
  stage3 stage3_1 (
    .Clock(clock_1_out), .Connection(t_ff_1_q), .Reset(button_3_out), .A1(stage2_1_a1), .A2(stage2_1_a2),
    .B3(stage3_1_b3), .out_7(stage3_1_out_7), .B1(stage3_1_b1), .B2(stage3_1_b2));
  stage4 stage4_1 (
    .B2(stage3_1_b2), .B1(stage3_1_b1), .B3(stage3_1_b3), .Connection(t_ff_1_q), .Clock(clock_1_out),
    .Reset(stage4_1_reset), .out_7(stage4_1_out_7), .C1(stage4_1_c1), .C2(stage4_1_c2));
  stage4 stage4_2 (
    .B2(stage4_1_c2), .B1(stage4_1_c1), .B3(stage4_1_reset), .Connection(t_ff_1_q), .Clock(clock_1_out),
    .out_7(stage4_2_out_7));  // open: Reset, C1, C2
  LED led_1 ();  // open: in
  Hex_Digit_Display hex_digit_display_1 (.value(stage4_2_out_7));  // open: dp
  Hex_Digit_Display hex_digit_display_2 (.value(stage4_1_out_7));  // open: dp
  Hex_Digit_Display hex_digit_display_3 (.value(stage3_1_out_7));  // open: dp
  Hex_Digit_Display hex_digit_display_4 (.value(stage2_1_out_4));  // open: dp
  Hex_Digit_Display hex_digit_display_5 ();  // open: value, dp
  Hex_Digit_Display hex_digit_display_6 ();  // open: value, dp
  Hex_Digit_Display hex_digit_display_7 ();  // open: value, dp
  Hex_Digit_Display hex_digit_display_8 ();  // open: value, dp

  // Notes on the sheet:
  //   Split
  //   Start/Stop
  //   Stopwatch Interface
  //   Reset
  //   Clock started
  //   Elapsed Time
  //   .
  //   .
  //   Split Time
  //   .
  //   .
endmodule

module stage2 (
  input  Reset,
  input  Connection,
  input  Clock,
  output [3:0] out_4,
  output A1,
  output A2
);

  wire and_1_out, and_2_out, and_3_out, and_4_out, and_5_out, j_k_ff_1_q, j_k_ff_3_q, or_1_out;

  J_K_Flip_Flop j_k_ff_1 (
    .J(Connection), .K(Connection), .clk(Clock), .Q(j_k_ff_1_q), .reset(or_1_out));  // open: Qn, preset
  and and_1 (and_1_out, Clock, Connection);
  and and_2 (and_2_out, Connection, j_k_ff_1_q);
  J_K_Flip_Flop j_k_ff_2 (.J(and_2_out), .K(and_2_out), .clk(Clock), .Q(A1), .reset(or_1_out));  // open: Qn, preset
  D_Flip_Flop d_ff_1 (.D(j_k_ff_1_q), .clk(and_1_out), .Q(out_4[0]));  // open: Qn, preset, reset
  and and_3 (and_3_out, and_2_out, A1);
  D_Flip_Flop d_ff_2 (.D(A1), .clk(and_1_out), .Q(out_4[1]));  // open: Qn, preset, reset
  J_K_Flip_Flop j_k_ff_3 (
    .J(and_3_out), .K(and_3_out), .clk(Clock), .Q(j_k_ff_3_q), .reset(or_1_out));  // open: Qn, preset
  and and_4 (and_4_out, and_3_out, j_k_ff_3_q);
  D_Flip_Flop d_ff_3 (.D(j_k_ff_3_q), .clk(and_1_out), .Q(out_4[2]));  // open: Qn, preset, reset
  J_K_Flip_Flop j_k_ff_4 (.J(and_4_out), .K(and_4_out), .clk(Clock), .Q(A2), .reset(or_1_out));  // open: Qn, preset
  D_Flip_Flop d_ff_4 (.D(A2), .clk(and_1_out), .Q(out_4[3]));  // open: Qn, preset, reset
  and and_5 (and_5_out, A1, A2);
  or or_1 (or_1_out, and_5_out, Reset);
endmodule

module stage3 (
  input  Clock,
  input  Connection,
  input  Reset,
  input  A1,
  input  A2,
  output B3,
  output [3:0] out_7,
  output B1,
  output B2
);

  wire and_1_out, and_2_out, and_3_out, and_4_out, j_k_ff_1_q, or_1_out;

  and and_1 (and_1_out, Clock, Connection);
  and and_2 (and_2_out, A1, A2);
  J_K_Flip_Flop j_k_ff_1 (
    .J(and_2_out), .K(and_2_out), .clk(and_2_out), .Q(j_k_ff_1_q), .reset(or_1_out));  // open: Qn, preset
  D_Flip_Flop d_ff_1 (.D(j_k_ff_1_q), .clk(and_1_out), .Q(out_7[0]), .reset(Reset));  // open: Qn, preset
  J_K_Flip_Flop j_k_ff_2 (
    .J(j_k_ff_1_q), .K(j_k_ff_1_q), .clk(and_2_out), .Q(B1), .reset(or_1_out));  // open: Qn, preset
  and and_3 (and_3_out, B1, j_k_ff_1_q);
  D_Flip_Flop d_ff_2 (.D(B1), .clk(and_1_out), .Q(out_7[1]), .reset(Reset));  // open: Qn, preset
  J_K_Flip_Flop j_k_ff_3 (.J(and_3_out), .K(and_3_out), .clk(and_2_out), .Q(B2), .reset(or_1_out));  // open: Qn, preset
  and and_4 (and_4_out, B2, B1);
  or or_1 (or_1_out, and_4_out, Reset);
  D_Flip_Flop d_ff_3 (.D(B2), .clk(and_1_out), .Q(out_7[2]), .reset(Reset));  // open: Qn, preset

  assign B3 = Reset;
  assign out_7[3] = 1'b0;
endmodule

module stage4 (
  input  B2,
  input  B1,
  input  B3,
  input  Connection,
  input  Clock,
  output Reset,
  output [3:0] out_7,
  output C1,
  output C2
);

  wire and_1_out, and_2_out, and_3_out, and_4_out, and_5_out, and_6_out, j_k_ff_1_q, j_k_ff_4_q, or_1_out;

  and and_1 (and_1_out, B2, B1);
  J_K_Flip_Flop j_k_ff_1 (.J(and_1_out), .K(and_1_out), .clk(and_1_out), .Q(j_k_ff_1_q));  // open: Qn, preset, reset
  and and_2 (and_2_out, Connection, Clock);
  and and_3 (and_3_out, j_k_ff_1_q, j_k_ff_1_q);
  D_Flip_Flop d_ff_1 (.D(j_k_ff_1_q), .clk(and_2_out), .Q(out_7[0]), .reset(B3));  // open: Qn, preset
  J_K_Flip_Flop j_k_ff_2 (.J(and_3_out), .K(and_3_out), .clk(and_1_out), .Q(C1), .reset(or_1_out));  // open: Qn, preset
  D_Flip_Flop d_ff_2 (.D(C1), .clk(and_2_out), .Q(out_7[1]), .reset(B3));  // open: Qn, preset
  and and_4 (and_4_out, C1, and_3_out);
  J_K_Flip_Flop j_k_ff_3 (.J(and_4_out), .K(and_4_out), .clk(and_1_out), .Q(C2), .reset(or_1_out));  // open: Qn, preset
  D_Flip_Flop d_ff_3 (.D(C2), .clk(and_2_out), .Q(out_7[2]), .reset(B3));  // open: Qn, preset
  and and_5 (and_5_out, C2, and_4_out);
  J_K_Flip_Flop j_k_ff_4 (
    .J(and_5_out), .K(and_5_out), .clk(and_1_out), .Q(j_k_ff_4_q), .reset(or_1_out));  // open: Qn, preset
  D_Flip_Flop d_ff_4 (.D(j_k_ff_4_q), .clk(and_2_out), .Q(out_7[3]), .reset(B3));  // open: Qn, preset
  and and_6 (and_6_out, j_k_ff_4_q, C1);
  or or_1 (or_1_out, and_6_out, B3);

  assign Reset = B3;
endmodule
