// Logisim project stage6.circ.circ as structural Verilog: 6 circuits, main circuit main
module main (
);

  wire button_1_out, button_2_out, button_3_out, clock_1_out, stage2_1_a1, stage2_1_a2, stage2_1_bit1,
       stage2_1_bit2, stage2_1_bit3, stage2_1_bit4, stage3_1_b1, stage3_1_b2, stage3_1_b3, stage3_1_bit1,
       stage3_1_bit2, stage3_1_bit3, stage4_1_bit1, stage4_1_bit2, stage4_1_bit3, stage4_1_bit4, stage4_1_c1,
       stage4_1_c2, stage4_1_reset, stage4_2_bit1, stage4_2_bit2, stage4_2_bit3, stage4_2_bit4,
       stage5_1_1_bit1out, stage5_1_1_bit2out, stage5_1_1_bit3out, stage5_1_1_bit4out, stage5_1_2_bit1out,
       stage5_1_2_bit2out, stage5_1_2_bit3out, stage5_1_2_bit4out, stage5_1_3_bit1out, stage5_1_3_bit2out,
       stage5_1_3_bit3out, stage5_1_3_bit4out, stage5_1_4_bit1out, stage5_1_4_bit2out, stage5_1_4_bit3out,
       stage5_1_4_bit4out, stage5_1_5_bit1out, stage5_1_5_bit2out, stage5_1_5_bit3out, stage5_1_5_bit4out,
       stage5_1_6_bit1out, stage5_1_6_bit2out, stage5_1_6_bit3out, stage5_1_6_bit4out, stage5_1_7_bit1out,
       stage5_1_7_bit2out, stage5_1_7_bit3out, stage5_1_7_bit4out, stage5_1_8_bit1out, stage5_1_8_bit2out,
       stage5_1_8_bit3out, stage5_1_8_bit4out, stage5_1_9_bit1out, stage5_1_9_bit2out, stage5_1_9_bit3out,
       stage5_1_9_bit4out, stage5_2_1_bit1out, stage5_2_1_bit2out, stage5_2_1_bit3out, stage5_2_2_bit1out,
       stage5_2_2_bit2out, stage5_2_2_bit3out, stage5_2_3_bit1out, stage5_2_3_bit2out, stage5_2_3_bit3out,
       t_ff_1_q;
  wire [3:0] stage2_1_out_4, stage3_1_out_7, stage4_1_out_7, stage4_2_out_7, stage5_1_1_out_11,
       stage5_1_2_out_11, stage5_1_3_out_11, stage5_1_4_out_11, stage5_1_5_out_11, stage5_1_6_out_11,
       stage5_1_7_out_11, stage5_1_8_out_11, stage5_1_9_out_11, stage5_1_10_out_11, stage5_1_11_out_11,
       stage5_1_12_out_11, stage5_2_1_out_9, stage5_2_2_out_9, stage5_2_3_out_9, stage5_2_4_out_9;

  Button button_1 (.out(button_1_out));
  Clock clock_1 (.out(clock_1_out));
  Button button_2 (.out(button_2_out));
  T_Flip_Flop t_ff_1 (.T(button_2_out), .clk(button_2_out), .Q(t_ff_1_q));  // open: Qn, reset, preset
  Button button_3 (.out(button_3_out));
  stage2 stage2_1 (
    .Reset(button_3_out), .Connection(t_ff_1_q), .Clock(clock_1_out), .out_4(stage2_1_out_4),
    .A1(stage2_1_a1), .A2(stage2_1_a2), .Bit1(stage2_1_bit1), .Bit3(stage2_1_bit3), .Bit2(stage2_1_bit2),
    .Bit4(stage2_1_bit4));
  stage3 stage3_1 (
    .Clock(clock_1_out), .Connection(t_ff_1_q), .Reset(button_3_out), .A1(stage2_1_a1), .A2(stage2_1_a2),
    .B3(stage3_1_b3), .out_7(stage3_1_out_7), .B1(stage3_1_b1), .Bit2(stage3_1_bit2), .B2(stage3_1_b2),
    .Bit1(stage3_1_bit1), .Bit3(stage3_1_bit3));
  stage4 stage4_1 (
    .B2(stage3_1_b2), .B1(stage3_1_b1), .B3(stage3_1_b3), .Connection(t_ff_1_q), .Clock(clock_1_out),
    .Reset(stage4_1_reset), .out_7(stage4_1_out_7), .C1(stage4_1_c1), .C2(stage4_1_c2), .Bit1(stage4_1_bit1),
    .Bit2(stage4_1_bit2), .Bit3(stage4_1_bit3), .Bit4(stage4_1_bit4));
  stage4 stage4_2 (
    .B2(stage4_1_c2), .B1(stage4_1_c1), .B3(stage4_1_reset), .Connection(t_ff_1_q), .Clock(clock_1_out),
    .out_7(stage4_2_out_7), .Bit1(stage4_2_bit1), .Bit2(stage4_2_bit2), .Bit3(stage4_2_bit3),
    .Bit4(stage4_2_bit4));  // open: Reset, C1, C2
  LED led_1 ();  // open: in
  Hex_Digit_Display hex_digit_display_1 (.value(stage4_2_out_7));  // open: dp
  Hex_Digit_Display hex_digit_display_2 (.value(stage4_1_out_7));  // open: dp
  Hex_Digit_Display hex_digit_display_3 (.value(stage3_1_out_7));  // open: dp
  Hex_Digit_Display hex_digit_display_4 (.value(stage2_1_out_4));  // open: dp
  stage5_1 stage5_1_1 (
    .Bit1(stage2_1_bit1), .Bit2(stage2_1_bit2), .Bit3(stage2_1_bit3), .Bit4(stage2_1_bit4),
    .Reset(button_3_out), .Split(button_1_out), .Bit4out(stage5_1_1_bit4out), .Bit3out(stage5_1_1_bit3out),
    .Bit2out(stage5_1_1_bit2out), .Bit1out(stage5_1_1_bit1out), .out_11(stage5_1_1_out_11));
  stage5_2 stage5_2_1 (
    .Bit1(stage3_1_bit1), .Bit2(stage3_1_bit2), .Bit3(stage3_1_bit3), .Reset(button_3_out),
    .Split(button_1_out), .Bit3Out(stage5_2_1_bit3out), .Bit2out(stage5_2_1_bit2out),
    .Bit1out(stage5_2_1_bit1out), .out_9(stage5_2_1_out_9));
  stage5_1 stage5_1_2 (
    .Bit1(stage4_1_bit1), .Bit2(stage4_1_bit2), .Bit3(stage4_1_bit3), .Bit4(stage4_1_bit4),
    .Reset(button_3_out), .Split(button_1_out), .Bit4out(stage5_1_2_bit4out), .Bit3out(stage5_1_2_bit3out),
    .Bit2out(stage5_1_2_bit2out), .Bit1out(stage5_1_2_bit1out), .out_11(stage5_1_2_out_11));
  stage5_1 stage5_1_3 (
    .Bit1(stage4_2_bit1), .Bit2(stage4_2_bit2), .Bit3(stage4_2_bit3), .Bit4(stage4_2_bit4),
    .Reset(button_3_out), .Split(button_1_out), .Bit4out(stage5_1_3_bit4out), .Bit3out(stage5_1_3_bit3out),
    .Bit2out(stage5_1_3_bit2out), .Bit1out(stage5_1_3_bit1out), .out_11(stage5_1_3_out_11));
  Hex_Digit_Display hex_digit_display_5 (.value(stage5_1_3_out_11));  // open: dp
  Hex_Digit_Display hex_digit_display_6 (.value(stage5_1_2_out_11));  // open: dp
  Hex_Digit_Display hex_digit_display_7 (.value(stage5_2_1_out_9));  // open: dp
  Hex_Digit_Display hex_digit_display_8 (.value(stage5_1_1_out_11));  // open: dp
  stage5_1 stage5_1_4 (
    .Bit1(stage5_1_1_bit1out), .Bit2(stage5_1_1_bit2out), .Bit3(stage5_1_1_bit3out),
    .Bit4(stage5_1_1_bit4out), .Reset(button_3_out), .Split(button_1_out), .Bit4out(stage5_1_4_bit4out),
    .Bit3out(stage5_1_4_bit3out), .Bit2out(stage5_1_4_bit2out), .Bit1out(stage5_1_4_bit1out),
    .out_11(stage5_1_4_out_11));
  stage5_2 stage5_2_2 (
    .Bit1(stage5_2_1_bit1out), .Bit2(stage5_2_1_bit2out), .Bit3(stage5_2_1_bit3out), .Reset(button_3_out),
    .Split(button_1_out), .Bit3Out(stage5_2_2_bit3out), .Bit2out(stage5_2_2_bit2out),
    .Bit1out(stage5_2_2_bit1out), .out_9(stage5_2_2_out_9));
  stage5_1 stage5_1_5 (
    .Bit1(stage5_1_2_bit1out), .Bit2(stage5_1_2_bit2out), .Bit3(stage5_1_2_bit3out),
    .Bit4(stage5_1_2_bit4out), .Reset(button_3_out), .Split(button_1_out), .Bit4out(stage5_1_5_bit4out),
    .Bit3out(stage5_1_5_bit3out), .Bit2out(stage5_1_5_bit2out), .Bit1out(stage5_1_5_bit1out),
    .out_11(stage5_1_5_out_11));
  stage5_1 stage5_1_6 (
    .Bit1(stage5_1_3_bit1out), .Bit2(stage5_1_3_bit2out), .Bit3(stage5_1_3_bit3out),
    .Bit4(stage5_1_3_bit4out), .Reset(button_3_out), .Split(button_1_out), .Bit4out(stage5_1_6_bit4out),
    .Bit3out(stage5_1_6_bit3out), .Bit2out(stage5_1_6_bit2out), .Bit1out(stage5_1_6_bit1out),
    .out_11(stage5_1_6_out_11));
  Hex_Digit_Display hex_digit_display_9 (.value(stage5_1_6_out_11));  // open: dp
  Hex_Digit_Display hex_digit_display_10 (.value(stage5_1_5_out_11));  // open: dp
  Hex_Digit_Display hex_digit_display_11 (.value(stage5_2_2_out_9));  // open: dp
  Hex_Digit_Display hex_digit_display_12 (.value(stage5_1_4_out_11));  // open: dp
  stage5_1 stage5_1_7 (
    .Bit1(stage5_1_4_bit1out), .Bit2(stage5_1_4_bit2out), .Bit3(stage5_1_4_bit3out),
    .Bit4(stage5_1_4_bit4out), .Reset(button_3_out), .Split(button_1_out), .Bit4out(stage5_1_7_bit4out),
    .Bit3out(stage5_1_7_bit3out), .Bit2out(stage5_1_7_bit2out), .Bit1out(stage5_1_7_bit1out),
    .out_11(stage5_1_7_out_11));
  stage5_2 stage5_2_3 (
    .Bit1(stage5_2_2_bit1out), .Bit2(stage5_2_2_bit2out), .Bit3(stage5_2_2_bit3out), .Reset(button_3_out),
    .Split(button_1_out), .Bit3Out(stage5_2_3_bit3out), .Bit2out(stage5_2_3_bit2out),
    .Bit1out(stage5_2_3_bit1out), .out_9(stage5_2_3_out_9));
  stage5_1 stage5_1_8 (
    .Bit1(stage5_1_5_bit1out), .Bit2(stage5_1_5_bit2out), .Bit3(stage5_1_5_bit3out),
    .Bit4(stage5_1_5_bit4out), .Reset(button_3_out), .Split(button_1_out), .Bit4out(stage5_1_8_bit4out),
    .Bit3out(stage5_1_8_bit3out), .Bit2out(stage5_1_8_bit2out), .Bit1out(stage5_1_8_bit1out),
    .out_11(stage5_1_8_out_11));
  stage5_1 stage5_1_9 (
    .Bit1(stage5_1_6_bit1out), .Bit2(stage5_1_6_bit2out), .Bit3(stage5_1_6_bit3out),
    .Bit4(stage5_1_6_bit4out), .Reset(button_3_out), .Split(button_1_out), .Bit4out(stage5_1_9_bit4out),
    .Bit3out(stage5_1_9_bit3out), .Bit2out(stage5_1_9_bit2out), .Bit1out(stage5_1_9_bit1out),
    .out_11(stage5_1_9_out_11));
  Hex_Digit_Display hex_digit_display_13 (.value(stage5_1_9_out_11));  // open: dp
  Hex_Digit_Display hex_digit_display_14 (.value(stage5_1_8_out_11));  // open: dp
  Hex_Digit_Display hex_digit_display_15 (.value(stage5_2_3_out_9));  // open: dp
  Hex_Digit_Display hex_digit_display_16 (.value(stage5_1_7_out_11));  // open: dp
  stage5_1 stage5_1_10 (
    .Bit1(stage5_1_7_bit1out), .Bit2(stage5_1_7_bit2out), .Bit3(stage5_1_7_bit3out),
    .Bit4(stage5_1_7_bit4out), .Reset(button_3_out), .Split(button_1_out), .out_11(stage5_1_10_out_11));  // open: Bit4out, Bit3out, Bit2out, Bit1out
  stage5_2 stage5_2_4 (
    .Bit1(stage5_2_3_bit1out), .Bit2(stage5_2_3_bit2out), .Bit3(stage5_2_3_bit3out), .Reset(button_3_out),
    .Split(button_1_out), .out_9(stage5_2_4_out_9));  // open: Bit3Out, Bit2out, Bit1out
  stage5_1 stage5_1_11 (
    .Bit1(stage5_1_8_bit1out), .Bit2(stage5_1_8_bit2out), .Bit3(stage5_1_8_bit3out),
    .Bit4(stage5_1_8_bit4out), .Reset(button_3_out), .Split(button_1_out), .out_11(stage5_1_11_out_11));  // open: Bit4out, Bit3out, Bit2out, Bit1out
  stage5_1 stage5_1_12 (
    .Bit1(stage5_1_9_bit1out), .Bit2(stage5_1_9_bit2out), .Bit3(stage5_1_9_bit3out),
    .Bit4(stage5_1_9_bit4out), .Reset(button_3_out), .Split(button_1_out), .out_11(stage5_1_12_out_11));  // open: Bit4out, Bit3out, Bit2out, Bit1out
  Hex_Digit_Display hex_digit_display_17 (.value(stage5_1_12_out_11));  // open: dp
  Hex_Digit_Display hex_digit_display_18 (.value(stage5_1_11_out_11));  // open: dp
  Hex_Digit_Display hex_digit_display_19 (.value(stage5_2_4_out_9));  // open: dp
  Hex_Digit_Display hex_digit_display_20 (.value(stage5_1_10_out_11));  // open: dp

  // Notes on the sheet:
  //   Split
  //   Start/Stop
  //   Stopwatch Interface
  //   Reset
  //   Clock started
  //   Elapsed Time
  //   .
  //   .
  //   Split Time
  //   .
  //   .
  //   Split Time
  //   .
  //   .
  //   Split Time
  //   .
  //   .
  //   Split Time
  //   .
  //   .
endmodule

module stage2 (
  input  Reset,
  input  Connection,
  input  Clock,
  output [3:0] out_4,
  output A1,
  output A2,
  output Bit1,
  output Bit3,
  output Bit2,
  output Bit4
);

  wire and_1_out, and_2_out, and_3_out, and_4_out, and_5_out, j_k_ff_1_q, j_k_ff_3_q, or_1_out;

  J_K_Flip_Flop j_k_ff_1 (
    .J(Connection), .K(Connection), .clk(Clock), .Q(j_k_ff_1_q), .reset(or_1_out));  // open: Qn, preset
  and and_1 (and_1_out, Clock, Connection);
  and and_2 (and_2_out, Connection, j_k_ff_1_q);
  J_K_Flip_Flop j_k_ff_2 (.J(and_2_out), .K(and_2_out), .clk(Clock), .Q(A1), .reset(or_1_out));  // open: Qn, preset
  D_Flip_Flop d_ff_1 (.D(j_k_ff_1_q), .clk(and_1_out), .Q(Bit1));  // open: Qn, preset, reset
  and and_3 (and_3_out, and_2_out, A1);
  D_Flip_Flop d_ff_2 (.D(A1), .clk(and_1_out), .Q(Bit2));  // open: Qn, preset, reset
  J_K_Flip_Flop j_k_ff_3 (
    .J(and_3_out), .K(and_3_out), .clk(Clock), .Q(j_k_ff_3_q), .reset(or_1_out));  // open: Qn, preset
  and and_4 (and_4_out, and_3_out, j_k_ff_3_q);
  D_Flip_Flop d_ff_3 (.D(j_k_ff_3_q), .clk(and_1_out), .Q(Bit3));  // open: Qn, preset, reset
  J_K_Flip_Flop j_k_ff_4 (.J(and_4_out), .K(and_4_out), .clk(Clock), .Q(A2), .reset(or_1_out));  // open: Qn, preset
  D_Flip_Flop d_ff_4 (.D(A2), .clk(and_1_out), .Q(Bit4));  // open: Qn, preset, reset
  and and_5 (and_5_out, A1, A2);
  or or_1 (or_1_out, and_5_out, Reset);

  assign out_4 = {Bit4, Bit3, Bit2, Bit1};
endmodule

module stage3 (
  input  Clock,
  input  Connection,
  input  Reset,
  input  A1,
  input  A2,
  output B3,
  output [3:0] out_7,
  output B1,
  output Bit2,
  output B2,
  output Bit1,
  output Bit3
);

  wire and_1_out, and_2_out, and_3_out, and_4_out, j_k_ff_1_q, or_1_out;

  and and_1 (and_1_out, Clock, Connection);
  and and_2 (and_2_out, A1, A2);
  J_K_Flip_Flop j_k_ff_1 (
    .J(and_2_out), .K(and_2_out), .clk(and_2_out), .Q(j_k_ff_1_q), .reset(or_1_out));  // open: Qn, preset
  D_Flip_Flop d_ff_1 (.D(j_k_ff_1_q), .clk(and_1_out), .Q(Bit1), .reset(Reset));  // open: Qn, preset
  J_K_Flip_Flop j_k_ff_2 (
    .J(j_k_ff_1_q), .K(j_k_ff_1_q), .clk(and_2_out), .Q(B1), .reset(or_1_out));  // open: Qn, preset
  and and_3 (and_3_out, B1, j_k_ff_1_q);
  D_Flip_Flop d_ff_2 (.D(B1), .clk(and_1_out), .Q(Bit2), .reset(Reset));  // open: Qn, preset
  J_K_Flip_Flop j_k_ff_3 (.J(and_3_out), .K(and_3_out), .clk(and_2_out), .Q(B2), .reset(or_1_out));  // open: Qn, preset
  and and_4 (and_4_out, B2, B1);
  or or_1 (or_1_out, and_4_out, Reset);
  D_Flip_Flop d_ff_3 (.D(B2), .clk(and_1_out), .Q(Bit3), .reset(Reset));  // open: Qn, preset

  assign B3 = Reset;
  assign out_7 = {1'b0, Bit3, Bit2, Bit1};
endmodule

module stage4 (
  input  B2,
  input  B1,
  input  B3,
  input  Connection,
  input  Clock,
  output Reset,
  output [3:0] out_7,
  output C1,
  output C2,
  output Bit1,
  output Bit2,
  output Bit3,
  output Bit4
);

  wire and_1_out, and_2_out, and_3_out, and_4_out, and_5_out, and_6_out, j_k_ff_1_q, j_k_ff_4_q, or_1_out;

  and and_1 (and_1_out, B2, B1);
  J_K_Flip_Flop j_k_ff_1 (.J(and_1_out), .K(and_1_out), .clk(and_1_out), .Q(j_k_ff_1_q));  // open: Qn, preset, reset
  and and_2 (and_2_out, Connection, Clock);
  and and_3 (and_3_out, j_k_ff_1_q, j_k_ff_1_q);
  D_Flip_Flop d_ff_1 (.D(j_k_ff_1_q), .clk(and_2_out), .Q(Bit1), .reset(B3));  // open: Qn, preset
  J_K_Flip_Flop j_k_ff_2 (.J(and_3_out), .K(and_3_out), .clk(and_1_out), .Q(C1), .reset(or_1_out));  // open: Qn, preset
  D_Flip_Flop d_ff_2 (.D(C1), .clk(and_2_out), .Q(Bit2), .reset(B3));  // open: Qn, preset
  and and_4 (and_4_out, C1, and_3_out);
  J_K_Flip_Flop j_k_ff_3 (.J(and_4_out), .K(and_4_out), .clk(and_1_out), .Q(C2), .reset(or_1_out));  // open: Qn, preset
  D_Flip_Flop d_ff_3 (.D(C2), .clk(and_2_out), .Q(Bit3), .reset(B3));  // open: Qn, preset
  and and_5 (and_5_out, C2, and_4_out);
  J_K_Flip_Flop j_k_ff_4 (
    .J(and_5_out), .K(and_5_out), .clk(and_1_out), .Q(j_k_ff_4_q), .reset(or_1_out));  // open: Qn, preset
  D_Flip_Flop d_ff_4 (.D(j_k_ff_4_q), .clk(and_2_out), .Q(Bit4), .reset(B3));  // open: Qn, preset
  and and_6 (and_6_out, j_k_ff_4_q, C1);
  or or_1 (or_1_out, and_6_out, B3);

  assign out_7 = {Bit4, Bit3, Bit2, Bit1};
  assign Reset = B3;
endmodule

module stage5_1 (
  input  Bit1,
  input  Bit2,
  input  Bit3,
  input  Bit4,
  input  Reset,
  input  Split,
  output Bit4out,
  output Bit3out,
  output Bit2out,
  output Bit1out,
  output [3:0] out_11
);

  D_Flip_Flop d_ff_1 (.D(Bit1), .clk(Split), .Q(Bit1out), .reset(Reset));  // open: Qn, preset
  D_Flip_Flop d_ff_2 (.D(Bit2), .clk(Split), .Q(Bit2out), .reset(Reset));  // open: Qn, preset
  D_Flip_Flop d_ff_3 (.D(Bit3), .clk(Split), .Q(Bit3out), .reset(Reset));  // open: Qn, preset
  D_Flip_Flop d_ff_4 (.D(Bit4), .clk(Split), .Q(Bit4out), .reset(Reset));  // open: Qn, preset

  assign out_11 = {Bit4out, Bit3out, Bit2out, Bit1out};
endmodule

module stage5_2 (
  input  Bit1,
  input  Bit2,
  input  Bit3,
  input  Reset,
  input  Split,
  output Bit3Out,
  output Bit2out,
  output Bit1out,
  output [3:0] out_9
);

  D_Flip_Flop d_ff_1 (.D(Bit1), .clk(Split), .Q(Bit1out), .reset(Reset));  // open: Qn, preset
  D_Flip_Flop d_ff_2 (.D(Bit2), .clk(Split), .Q(Bit2out), .reset(Reset));  // open: Qn, preset
  D_Flip_Flop d_ff_3 (.D(Bit3), .clk(Split), .Q(Bit3Out), .reset(Reset));  // open: Qn, preset

  assign out_9 = {1'b0, Bit3Out, Bit2out, Bit1out};
endmodule
